# Fritzing sketch Pushbutton Piano (saved by Fritzing 0.9.2b)
breadboards: 1

parts:
  S1 = Pushbutton [package="[THT]"]
  S2 = Pushbutton [package="[THT]"]
  S3 = Pushbutton [package="[THT]"]
  S4 = Pushbutton [package="[THT]"]
  S5 = Pushbutton [package="[THT]"]
  R1 = Resistor [tolerance=±5% resistance=220 package=THT]
  Part1 = Arduino Uno (Rev3)
  R2 = Resistor [tolerance=±5% resistance=220 package=THT]
  R3 = Resistor [tolerance=±5% resistance=220 package=THT]
  R4 = Resistor [tolerance=±5% resistance=220 package=THT]
  R5 = Resistor [tolerance=±5% resistance=220 package=THT]
  J1 = Piezo Speaker

nets:
  N1: S1.Pin_1, S1.Pin_2, S2.Pin_1, S2.Pin_2, S3.Pin_1, S3.Pin_2, S4.Pin_1, S4.Pin_2, S5.Pin_1, S5.Pin_2, Part1.5V
  N2: S1.Pin_3, S1.Pin_4, R1.Pin_1, Part1.D2
  N3: S2.Pin_3, S2.Pin_4, Part1.D3_PWM, R2.Pin_1
  N4: S3.Pin_3, S3.Pin_4, Part1.D4, R3.Pin_1
  N5: S4.Pin_3, S4.Pin_4, Part1.D5_PWM, R4.Pin_1
  N6: S5.Pin_3, S5.Pin_4, Part1.D6_PWM, R5.Pin_1
  N7: R1.Pin_0, Part1.GND, R2.Pin_0, R3.Pin_0, R4.Pin_0, R5.Pin_0, J1.pin1
  N8: Part1.D9_PWM, J1.pin2
